# Fritzing sketch wheel-sensor-wiring (saved by Fritzing 0.9.3b)
breadboards: 1

parts:
  Adafruit_HUZZAH_ESP8266_Breakout1 = Adafruit HUZZAH ESP8266 Breakout [part_number=2471]
  Q1 = PHOTOTRANSISTOR REFLECTIVE OBJECT SENSOR [package=qrb1114-side]
  R1 = Resistor [tolerance=±5% resistance=220 package=THT]
  R2 = Resistor [tolerance=±5% resistance=10k package="0402 [SMD]"]

nets:
  N1: Adafruit_HUZZAH_ESP8266_Breakout1.GND, Q1.C, R1.Pin_0
  N2: Adafruit_HUZZAH_ESP8266_Breakout1.#13, Q1.E
  N3: Adafruit_HUZZAH_ESP8266_Breakout1.#12, Q1.A
  N4: Adafruit_HUZZAH_ESP8266_Breakout1.3V, R2.Pin_1
  N5: Q1.K, R1.Pin_1
